// Logisim project ALU.circ as structural Verilog: 1 circuit, main circuit main
module main (
  input  Cin,
  input  [7:0] in_2,
  input  [7:0] in_3,
  input  [1:0] S1_S0,
  input  S2,
  output [7:0] Y
);

  wire [7:0] adder_1_out, and_1_out, multiplexer_1_out, multiplexer_2_out, not_1_out, not_2_out, or_1_out,
       xor_1_out;

  assign not_1_out = ~in_3;  // NOT_Gate not_1, 8 bits wide
  Multiplexer #(.select(2), .width(8), .enable("false")) multiplexer_1 (
    .in0(in_3), .in1(not_1_out), .in2({8{1'b0}}), .in3({8{1'b1}}), .out(multiplexer_1_out), .sel(S1_S0));
  assign and_1_out = in_2 & in_3;  // AND_Gate and_1, 8 bits wide
  assign or_1_out = in_2 | in_3;  // OR_Gate or_1, 8 bits wide
  assign not_2_out = ~in_2;  // NOT_Gate not_2, 8 bits wide
  assign xor_1_out = in_2 ^ in_3;  // XOR_Gate xor_1, 8 bits wide
  Adder adder_1 (.a(in_2), .b(multiplexer_1_out), .out(adder_1_out), .cin(Cin));  // open: cout
  Multiplexer #(.select(2), .width(8), .enable("false")) multiplexer_2 (
    .in0(and_1_out), .in1(or_1_out), .in2(not_2_out), .in3(xor_1_out), .out(multiplexer_2_out), .sel(S1_S0));
  Multiplexer #(.width(8), .enable("false")) multiplexer_3 (
    .in0(adder_1_out), .in1(multiplexer_2_out), .out(Y), .sel(S2));

  // Notes on the sheet:
  //   A
  //   B
  //   D
endmodule
