// Logisim project AlgorithmUnit.circ as structural Verilog: 1 circuit, main circuit main
module main (
  input  Cin,
  input  [7:0] in_2,
  input  [7:0] in_3,
  input  [1:0] S1_S0,
  output [7:0] out_5
);

  wire [7:0] multiplexer_1_out, not_1_out;

  assign not_1_out = ~in_3;  // NOT_Gate not_1, 8 bits wide
  Multiplexer #(.select(2), .width(8), .enable("false")) multiplexer_1 (
    .in0(in_3), .in1(not_1_out), .in2({8{1'b0}}), .in3({8{1'b1}}), .out(multiplexer_1_out), .sel(S1_S0));
  Adder adder_1 (.a(in_2), .b(multiplexer_1_out), .out(out_5), .cin(Cin));  // open: cout

  // Notes on the sheet:
  //   A
  //   B
  //   D
endmodule
