// Logisim project FunctionUnit.circ as structural Verilog: 1 circuit, main circuit main
module main (
  input  IL,
  input  IR,
  input  [1:0] SH,
  input  Cin,
  input  [7:0] in_5,
  input  [7:0] in_6,
  input  [1:0] S1_S0,
  input  S2,
  input  S4,
  output SOL,
  output SOR,
  output [7:0] Y
);

  wire [7:0] adder_1_out, and_1_out, multiplexer_1_out, multiplexer_2_out, multiplexer_3_out,
       multiplexer_5_out, not_1_out, not_2_out, or_1_out, xor_1_out;

  assign not_1_out = ~in_6;  // NOT_Gate not_1, 8 bits wide
  Multiplexer #(.select(2), .width(8), .enable("false")) multiplexer_1 (
    .in0(in_6), .in1(not_1_out), .in2({8{1'b0}}), .in3({8{1'b1}}), .out(multiplexer_1_out), .sel(S1_S0));
  assign and_1_out = in_5 & in_6;  // AND_Gate and_1, 8 bits wide
  assign or_1_out = in_5 | in_6;  // OR_Gate or_1, 8 bits wide
  assign not_2_out = ~in_5;  // NOT_Gate not_2, 8 bits wide
  assign xor_1_out = in_5 ^ in_6;  // XOR_Gate xor_1, 8 bits wide
  Adder adder_1 (.a(in_5), .b(multiplexer_1_out), .out(adder_1_out), .cin(Cin));  // open: cout
  Multiplexer #(.select(2), .width(8), .enable("false")) multiplexer_2 (
    .in0(and_1_out), .in1(or_1_out), .in2(not_2_out), .in3(xor_1_out), .out(multiplexer_2_out), .sel(S1_S0));
  Multiplexer #(.select(2), .width(8), .enable("false")) multiplexer_3 (
    .in0(in_6), .in1({in_6[6:0], IL}), .in2({IR, in_6[7:1]}), .out(multiplexer_3_out), .sel(SH));  // open: in3
  Multiplexer #(.width(8), .enable("false")) multiplexer_4 (
    .in0(multiplexer_3_out), .in1(multiplexer_5_out), .out(Y), .sel(S4));
  Multiplexer #(.width(8), .enable("false")) multiplexer_5 (
    .in0(adder_1_out), .in1(multiplexer_2_out), .out(multiplexer_5_out), .sel(S2));

  assign SOL = in_6[7];
  assign SOR = in_6[0];

  // Notes on the sheet:
  //   A
  //   B
  //   D
endmodule
