// Logisim project FunctionUnit_Finish.circ as structural Verilog: 1 circuit, main circuit FunctionUnit
module FunctionUnit (
  input  Cin,
  input  [7:0] in_2,
  input  [7:0] in_3,
  input  [1:0] S1_S0,
  input  S2,
  input  S3,
  output [7:0] Y,
  output OV,
  output SG,
  output CA,
  output ZO
);

  wire adder_1_cout, adder_2_cout, multiplexer_6_out;
  wire [6:0] adder_1_out;
  wire [7:0] and_1_out, multiplexer_1_out, multiplexer_2_out, multiplexer_3_out, multiplexer_5_out,
       not_1_out, not_2_out, or_1_out, xor_1_out;

  assign not_1_out = ~in_3;  // NOT_Gate not_1, 8 bits wide
  Multiplexer #(.select(2), .width(8), .enable("false")) multiplexer_1 (
    .in0(in_3), .in1(not_1_out), .in2({8{1'b0}}), .in3({8{1'b1}}), .out(multiplexer_1_out), .sel(S1_S0));
  assign and_1_out = in_2 & in_3;  // AND_Gate and_1, 8 bits wide
  assign or_1_out = in_2 | in_3;  // OR_Gate or_1, 8 bits wide
  assign not_2_out = ~in_2;  // NOT_Gate not_2, 8 bits wide
  assign xor_1_out = in_2 ^ in_3;  // XOR_Gate xor_1, 8 bits wide
  Adder #(.width(7)) adder_1 (
    .a(in_2[6:0]), .b(multiplexer_1_out[6:0]), .out(adder_1_out), .cin(Cin), .cout(adder_1_cout));
  Adder #(.width(1)) adder_2 (.a(in_2[7]), .b(multiplexer_1_out[7]), .out(SG), .cin(adder_1_cout), .cout(adder_2_cout));
  Multiplexer #(.select(2), .width(8), .enable("false")) multiplexer_2 (
    .in0(and_1_out), .in1(or_1_out), .in2(not_2_out), .in3(xor_1_out), .out(multiplexer_2_out), .sel(S1_S0));
  Multiplexer #(.select(2), .width(8), .enable("false")) multiplexer_3 (
    .in0(in_3), .in1({in_3[6:0], 1'b0}), .in2({1'b0, in_3[7:1]}), .in3({{2{in_3[7]}}, in_3[6:1]}),
    .out(multiplexer_3_out), .sel(S1_S0));
  Multiplexer #(.width(8), .enable("false")) multiplexer_4 (
    .in0(multiplexer_3_out), .in1(multiplexer_5_out), .out(Y), .sel(S3));
  Multiplexer #(.width(8), .enable("false")) multiplexer_5 (
    .in0({SG, adder_1_out}), .in1(multiplexer_2_out), .out(multiplexer_5_out), .sel(S2));
  Multiplexer #(.select(2), .enable("false")) multiplexer_6 (
    .in0(1'b0), .in1(in_3[7]), .in2(in_3[0]), .in3(in_3[0]), .out(multiplexer_6_out), .sel(S1_S0));
  xor xor_2 (OV, adder_1_cout, adder_2_cout);
  Multiplexer #(.enable("false")) multiplexer_7 (.in0(multiplexer_6_out), .in1(adder_2_cout), .out(CA), .sel(S3));
  nor nor_1 (ZO, multiplexer_5_out[0], multiplexer_5_out[1], multiplexer_5_out[2], multiplexer_5_out[3], multiplexer_5_out[4], multiplexer_5_out[5], multiplexer_5_out[6], multiplexer_5_out[7]);

  // Notes on the sheet:
  //   A
  //   B
  //   D
  //   SOL
  //   SOR
endmodule
