// Logisim project LogicUnit.circ as structural Verilog: 1 circuit, main circuit main
module main (
  input  Cin,
  input  [7:0] in_2,
  input  [7:0] in_3,
  input  [1:0] S1_S0,
  input  [7:0] A,
  input  [7:0] B,
  input  [1:0] S1_S0_2,
  output [7:0] out_8,
  output [7:0] Y
);

  wire [7:0] and_1_out, multiplexer_1_out, not_1_out, not_2_out, or_1_out, xor_1_out;

  assign not_1_out = ~in_3;  // NOT_Gate not_1, 8 bits wide
  Multiplexer #(.select(2), .width(8), .enable("false")) multiplexer_1 (
    .in0(in_3), .in1(not_1_out), .in2({8{1'b0}}), .in3({8{1'b1}}), .out(multiplexer_1_out), .sel(S1_S0));
  assign and_1_out = A & B;  // AND_Gate and_1, 8 bits wide
  assign or_1_out = A | B;  // OR_Gate or_1, 8 bits wide
  assign not_2_out = ~A;  // NOT_Gate not_2, 8 bits wide
  assign xor_1_out = A ^ B;  // XOR_Gate xor_1, 8 bits wide
  Adder adder_1 (.a(in_2), .b(multiplexer_1_out), .out(out_8), .cin(Cin));  // open: cout
  Multiplexer #(.select(2), .width(8), .enable("false")) multiplexer_2 (
    .in0(and_1_out), .in1(or_1_out), .in2(not_2_out), .in3(xor_1_out), .out(Y), .sel(S1_S0_2));

  // Notes on the sheet:
  //   A
  //   B
  //   D
endmodule
