// Logisim project shifter.circ as structural Verilog: 1 circuit, main circuit main
module main (
  input  \IL_移入端 ,
  input  [7:0] X,
  input  [7:0] X_2,
  input  S,
  input  \IL_左移入 ,
  input  [2:0] S_2,
  input  \IR_右移入 ,
  input  [7:0] X_3,
  input  [1:0] S_3,
  output [7:0] Y,
  output \SO移出端 ,
  output [7:0] Y_2,
  output [7:0] Y_3,
  output \SOL_左移出 ,
  output \SOR_右移出 
);

  Multiplexer #(.width(8), .enable("false")) multiplexer_1 (.in0(X), .in1({X[6:0], \IL_移入端 }), .out(Y), .sel(S));
  Multiplexer #(.select(2), .width(8), .enable("false")) multiplexer_2 (
    .in0(X_3), .in1({X_3[6:0], \IL_左移入 }), .in2({\IR_右移入 , X_3[7:1]}), .out(Y_3), .sel(S_3));  // open: in3
  Multiplexer #(.select(3), .width(8), .enable("false")) multiplexer_3 (
    .in0(X_2), .in1({X_2[6:0], X_2[7]}), .in2({X_2[5:0], X_2[7:6]}), .in3({X_2[4:0], X_2[7:5]}),
    .in4({X_2[3:0], X_2[7:4]}), .in5({X_2[2:0], X_2[7:3]}), .in6({X_2[1:0], X_2[7:2]}),
    .in7({X_2[0], X_2[7:1]}), .out(Y_2), .sel(S_2));

  assign \SOL_左移出  = X_3[7];
  assign \SOR_右移出  = X_3[0];
  assign \SO移出端  = X[7];

  // Notes on the sheet:
  //   S=00保持,S=01左移，S=10右移
endmodule
