// Logisim project CU.circ as structural Verilog: 2 circuits, main circuit CU
module CU (
  input  \TC_转到下一指令 ,
  input  RST,
  input  O,
  input  S,
  input  C,
  input  Z,
  input  \TA_执行指令 ,
  input  [15:0] \PDIN_程序数据 ,
  input  \TF_取指令 ,
  output [7:0] \PADDR_程序地址 ,
  output W,
  output CI,
  output RM,
  output WM,
  output SF,
  output JP,
  output [4:0] FS,
  output [7:0] ADDRIM
);

  wire and_1_out, multiplexer_1_out, nor_1_out;
  wire [3:0] register_1_q;
  wire [7:0] adder_1_out, multiplexer_2_out;

  Register #(.width(4)) register_1 (.D({Z, C, S, O}), .en(SF), .Q(register_1_q), .clk(\TA_执行指令 ));  // open: clr
  Register PC (.D(adder_1_out), .Q(\PADDR_程序地址 ), .clk(\TC_转到下一指令 ), .clr(RST));  // open: en
  Multiplexer #(.select(3), .enable("false")) multiplexer_1 (
    .in0(1'b1), .in1(register_1_q[0]), .in2(register_1_q[1]), .in3(register_1_q[2]), .in4(register_1_q[3]),
    .out(multiplexer_1_out), .sel(FS[3:1]));  // open: in5, in6, in7
  Register #(.width(16)) IR (.D(\PDIN_程序数据 ), .Q({JP, RM, CI, FS, ADDRIM}), .clk(\TF_取指令 ));  // open: en, clr
  Multiplexer #(.width(8), .enable("false")) multiplexer_2 (
    .in0(8'h1), .in1(ADDRIM), .out(multiplexer_2_out), .sel(and_1_out));
  and and_1 (and_1_out, multiplexer_1_out, JP);
  Adder adder_1 (.a(\PADDR_程序地址 ), .b(multiplexer_2_out), .out(adder_1_out));  // open: cin, cout
  nor nor_1 (nor_1_out, JP, RM);
  and and_2 (WM, RM, ~CI);  // AND_Gate
  nor nor_2 (SF, JP, RM);
  or or_1 (W, nor_1_out, CI);
endmodule

module OPdecoder (
  input  [15:0] IND,
  output W,
  output CI,
  output RM,
  output WM,
  output SF,
  output JP,
  output [4:0] OPCODE,
  output [7:0] ADDRIM
);

  wire nor_1_out;

  nor nor_1 (nor_1_out, IND[0], IND[1]);
  or or_1 (W, nor_1_out, IND[2]);
  and and_1 (WM, IND[1], ~IND[2]);  // AND_Gate
  nor nor_2 (SF, IND[0], IND[1]);

  assign ADDRIM = IND[15:8];
  assign CI = IND[2];
  assign JP = IND[0];
  assign OPCODE = IND[7:3];
  assign RM = IND[1];
endmodule
