// Logisim project withdevice.circ as structural Verilog: 1 circuit, main circuit main
module main (
  input  in_1,
  input  \Reset_重启 
);

  wire clock_1_out, cu_1_ci, cu_1_rm, cu_1_w, cu_1_wm, decoder_1_out0, decoder_1_out1, decoder_1_out2,
       decoder_1_out3;
  wire [1:0] counter_1_q, cu_1_addrim, cu_1_addrim_2, cu_1_addrim_3, cu_1_addrim_4;
  wire [3:0] functionunit_1_ov;
  wire [4:0] cu_1_fs;
  wire [7:0] bit_extender_1_out, \cu_1_paddr_程序地址 , functionunit_1_y, multiplexer_1_out, multiplexer_2_out,
       ram_1_data, \regs_1_a_待输出数据 , \regs_1_b_待输出数据 ;
  wire [15:0] rom_1_data;

  Clock clock_1 (.out(clock_1_out));
  // Probe on \cu_1_paddr_程序地址 
  Decoder #(.select(2), .enable("false")) decoder_1 (
    .out0(decoder_1_out0), .out1(decoder_1_out1), .out2(decoder_1_out2), .out3(decoder_1_out3),
    .sel(counter_1_q));
  Counter #(.width(2), .max('h3)) counter_1 (
    .Q(counter_1_q), .clk(clock_1_out), .clr(\Reset_重启 ));  // open: load, D, count, carry
  ROM #(.dataWidth(16)) rom_1 (.addr(\cu_1_paddr_程序地址 ), .data(rom_1_data), .sel(1'b1));
  // Probe on rom_1_data
  // Probe on multiplexer_2_out
  // Probe on \regs_1_a_待输出数据 
  // Probe on multiplexer_1_out
  Regs regs_1 (
    .\Din_待写入数据 (multiplexer_2_out), .\ADDR_选择寄存器 (cu_1_addrim_4), .\SB_B选择输出 (cu_1_addrim_2),
    .\nR_W是否写 (cu_1_w), .\SA_A选择输出 (cu_1_addrim_3), .\CLK时钟 (decoder_1_out3), .\A_待输出数据 (\regs_1_a_待输出数据 ),
    .\B_待输出数据 (\regs_1_b_待输出数据 ));
  assign bit_extender_1_out = {{4{1'b0}}, {cu_1_addrim_2, cu_1_addrim}};  // Bit_Extender bit_extender_1
  CU cu_1 (
    .RST(\Reset_重启 ), .\TC_转到下一指令 (decoder_1_out0), .\PDIN_程序数据 (rom_1_data), .\TF_取指令 (decoder_1_out1),
    .\PADDR_程序地址 (\cu_1_paddr_程序地址 ), .W(cu_1_w), .CI(cu_1_ci), .RM(cu_1_rm), .WM(cu_1_wm), .FS(cu_1_fs),
    .ADDRIM({cu_1_addrim_4, cu_1_addrim_3, cu_1_addrim_2, cu_1_addrim}), .O(functionunit_1_ov[0]),
    .S(functionunit_1_ov[1]), .C(functionunit_1_ov[2]), .Z(functionunit_1_ov[3]), .\TA_执行指令 (decoder_1_out3));  // open: SF, JP
  // Probe on {cu_1_addrim_4, cu_1_addrim_3, cu_1_addrim_2, cu_1_addrim}
  Multiplexer #(.width(8), .enable("false")) multiplexer_1 (
    .in0(\regs_1_b_待输出数据 ), .in1(bit_extender_1_out), .out(multiplexer_1_out), .sel(cu_1_ci));
  RAM #(.bus("separate")) ram_1 (
    .addr(\regs_1_a_待输出数据 ), .din(multiplexer_1_out), .data(ram_1_data), .str(cu_1_wm), .sel(1'b1),
    .clk(decoder_1_out2), .ld(1'b1), .clr(in_1));
  FunctionUnit functionunit_1 (
    .Cin(cu_1_fs[0]), .in_2(\regs_1_a_待输出数据 ), .in_3(multiplexer_1_out), .S1_S0(cu_1_fs[2:1]),
    .S2(cu_1_fs[3]), .S3(cu_1_fs[4]), .Y(functionunit_1_y), .ZO(functionunit_1_ov[3]),
    .CA(functionunit_1_ov[2]), .OV(functionunit_1_ov[0]), .SG(functionunit_1_ov[1]));
  Multiplexer #(.width(8), .enable("false")) multiplexer_2 (
    .in0(functionunit_1_y), .in1(ram_1_data), .out(multiplexer_2_out), .sel(cu_1_rm));

  // Notes on the sheet:
  //   contents of rom_1 (hex, n*v repeats v):
  //   2001 2041 20c0 1084 4038 15f0 4 48 80fb
endmodule
