// Logisim project ENDff.circ as structural Verilog: 1 circuit, main circuit main
module main (
  input  \C时钟 ,
  input  \D数据 ,
  input  \EN送数使能 ,
  output \Q输出 
);

  wire multiplexer_1_out;

  D_Flip_Flop d_ff_1 (.clk(\C时钟 ), .D(multiplexer_1_out), .Q(\Q输出 ));  // open: Qn, preset, en, reset
  Multiplexer #(.enable("false")) multiplexer_1 (.in0(\Q输出 ), .in1(\D数据 ), .out(multiplexer_1_out), .sel(\EN送数使能 ));
endmodule
