// Logisim project registers.circ as structural Verilog: 1 circuit, main circuit Regs
module Regs (
  input  [7:0] \Din_待写入数据 ,
  input  [1:0] \ADDR_选择寄存器 ,
  input  [1:0] \SB_B选择输出 ,
  input  \nR_W是否写 ,
  input  [1:0] \SA_A选择输出 ,
  input  \CLK时钟 ,
  output [7:0] \A_待输出数据 ,
  output [7:0] \B_待输出数据 
);

  wire and_1_out, and_2_out, and_3_out, and_4_out, decoder_1_out0, decoder_1_out1, decoder_1_out2,
       decoder_1_out3;
  wire [7:0] register_1_q, register_2_q, register_3_q, register_4_q;

  Decoder #(.select(2), .enable("false")) decoder_1 (
    .out0(decoder_1_out0), .out1(decoder_1_out1), .out2(decoder_1_out2), .out3(decoder_1_out3),
    .sel(\ADDR_选择寄存器 ));
  and and_1 (and_1_out, \nR_W是否写 , decoder_1_out0);
  and and_2 (and_2_out, \nR_W是否写 , decoder_1_out1);
  and and_3 (and_3_out, \nR_W是否写 , decoder_1_out2);
  and and_4 (and_4_out, \nR_W是否写 , decoder_1_out3);
  Register register_1 (.D(\Din_待写入数据 ), .en(and_1_out), .Q(register_1_q), .clk(\CLK时钟 ));  // open: clr
  Register register_2 (.D(\Din_待写入数据 ), .en(and_2_out), .Q(register_2_q), .clk(\CLK时钟 ));  // open: clr
  Register register_3 (.D(\Din_待写入数据 ), .en(and_3_out), .Q(register_3_q), .clk(\CLK时钟 ));  // open: clr
  Register register_4 (.D(\Din_待写入数据 ), .en(and_4_out), .Q(register_4_q), .clk(\CLK时钟 ));  // open: clr
  Multiplexer #(.select(2), .width(8), .enable("false")) multiplexer_1 (
    .in0(register_1_q), .in1(register_2_q), .in2(register_3_q), .in3(register_4_q), .out(\A_待输出数据 ),
    .sel(\SA_A选择输出 ));
  Multiplexer #(.select(2), .width(8), .enable("false")) multiplexer_2 (
    .in0(register_1_q), .in1(register_2_q), .in2(register_3_q), .in3(register_4_q), .out(\B_待输出数据 ),
    .sel(\SB_B选择输出 ));
endmodule
