// Logisim project rscpu.circ as structural Verilog
module AlgorithmUnit (
  input  Cin,
  input  [7:0] in_2,
  input  [7:0] in_3,
  input  [1:0] S1_S0,
  output [7:0] out_5
);

  wire [7:0] multiplexer_1_out, not_1_out;

  assign not_1_out = ~in_3;  // NOT_Gate not_1, 8 bits wide
  Multiplexer #(.select(2), .width(8), .enable("false")) multiplexer_1 (
    .in0(in_3), .in1(not_1_out), .in2({8{1'b0}}), .in3({8{1'b1}}), .out(multiplexer_1_out), .sel(S1_S0));
  Adder adder_1 (.a(in_2), .b(multiplexer_1_out), .out(out_5), .cin(Cin));  // open: cout

  // Notes on the sheet:
  //   A
  //   B
  //   D
endmodule

module LogicUnit (
  input  [7:0] A,
  input  [7:0] B,
  input  [1:0] S1_S0,
  output [7:0] Y
);

  wire [7:0] and_1_out, not_1_out, or_1_out, xor_1_out;

  assign not_1_out = ~A;  // NOT_Gate not_1, 8 bits wide
  assign and_1_out = A & B;  // AND_Gate and_1, 8 bits wide
  assign or_1_out = A | B;  // OR_Gate or_1, 8 bits wide
  assign xor_1_out = A ^ B;  // XOR_Gate xor_1, 8 bits wide
  Multiplexer #(.select(2), .width(8), .enable("false")) multiplexer_1 (
    .in0(and_1_out), .in1(or_1_out), .in2(not_1_out), .in3(xor_1_out), .out(Y), .sel(S1_S0));
endmodule

module ALU (
  input  Cin,
  input  [7:0] in_2,
  input  [7:0] in_3,
  input  [1:0] S1_S0,
  input  S2,
  output [7:0] Y
);

  wire [7:0] adder_1_out, and_1_out, multiplexer_1_out, multiplexer_2_out, not_1_out, not_2_out, or_1_out,
       xor_1_out;

  assign not_1_out = ~in_3;  // NOT_Gate not_1, 8 bits wide
  Multiplexer #(.select(2), .width(8), .enable("false")) multiplexer_1 (
    .in0(in_3), .in1(not_1_out), .in2({8{1'b0}}), .in3({8{1'b1}}), .out(multiplexer_1_out), .sel(S1_S0));
  assign and_1_out = in_2 & in_3;  // AND_Gate and_1, 8 bits wide
  assign or_1_out = in_2 | in_3;  // OR_Gate or_1, 8 bits wide
  assign not_2_out = ~in_2;  // NOT_Gate not_2, 8 bits wide
  assign xor_1_out = in_2 ^ in_3;  // XOR_Gate xor_1, 8 bits wide
  Adder adder_1 (.a(in_2), .b(multiplexer_1_out), .out(adder_1_out), .cin(Cin));  // open: cout
  Multiplexer #(.select(2), .width(8), .enable("false")) multiplexer_2 (
    .in0(and_1_out), .in1(or_1_out), .in2(not_2_out), .in3(xor_1_out), .out(multiplexer_2_out), .sel(S1_S0));
  Multiplexer #(.width(8), .enable("false")) multiplexer_3 (
    .in0(adder_1_out), .in1(multiplexer_2_out), .out(Y), .sel(S2));

  // Notes on the sheet:
  //   A
  //   B
  //   D
endmodule

module Shifter (
  input  \IL_移入端 ,
  input  [7:0] X,
  input  S,
  output [7:0] Y,
  output \SO移出端 
);

  Multiplexer #(.width(8), .enable("false")) multiplexer_1 (.in0(X), .in1({X[6:0], \IL_移入端 }), .out(Y), .sel(S));

  assign \SO移出端  = X[7];
endmodule

module BidShifter (
  input  \IL_左移入 ,
  input  \IR_右移入 ,
  input  [7:0] X,
  input  [1:0] S,
  output [7:0] Y,
  output \SOL_左移出 ,
  output \SOR_右移出 
);

  Multiplexer #(.select(2), .width(8), .enable("false")) multiplexer_1 (
    .in0(X), .in1({X[6:0], \IL_左移入 }), .in2({\IR_右移入 , X[7:1]}), .out(Y), .sel(S));  // open: in3

  assign \SOL_左移出  = X[7];
  assign \SOR_右移出  = X[0];

  // Notes on the sheet:
  //   S=00保持,S=01左移，S=10右移
endmodule

module BarrelShifter (
  input  [7:0] X,
  input  [2:0] S,
  output [7:0] Y
);

  Multiplexer #(.select(3), .width(8), .enable("false")) multiplexer_1 (
    .in0(X), .in1({X[6:0], X[7]}), .in2({X[5:0], X[7:6]}), .in3({X[4:0], X[7:5]}), .in4({X[3:0], X[7:4]}),
    .in5({X[2:0], X[7:3]}), .in6({X[1:0], X[7:2]}), .in7({X[0], X[7:1]}), .out(Y), .sel(S));
endmodule

module FunctionUnit (
  input  IL,
  input  IR,
  input  [1:0] SH,
  input  Cin,
  input  [7:0] in_5,
  input  [7:0] in_6,
  input  [1:0] S1_S0,
  input  S2,
  input  S4,
  output SOL,
  output SOR,
  output [7:0] Y
);

  wire [7:0] adder_1_out, and_1_out, multiplexer_1_out, multiplexer_2_out, multiplexer_3_out,
       multiplexer_5_out, not_1_out, not_2_out, or_1_out, xor_1_out;

  assign not_1_out = ~in_6;  // NOT_Gate not_1, 8 bits wide
  Multiplexer #(.select(2), .width(8), .enable("false")) multiplexer_1 (
    .in0(in_6), .in1(not_1_out), .in2({8{1'b0}}), .in3({8{1'b1}}), .out(multiplexer_1_out), .sel(S1_S0));
  assign and_1_out = in_5 & in_6;  // AND_Gate and_1, 8 bits wide
  assign or_1_out = in_5 | in_6;  // OR_Gate or_1, 8 bits wide
  assign not_2_out = ~in_5;  // NOT_Gate not_2, 8 bits wide
  assign xor_1_out = in_5 ^ in_6;  // XOR_Gate xor_1, 8 bits wide
  Adder adder_1 (.a(in_5), .b(multiplexer_1_out), .out(adder_1_out), .cin(Cin));  // open: cout
  Multiplexer #(.select(2), .width(8), .enable("false")) multiplexer_2 (
    .in0(and_1_out), .in1(or_1_out), .in2(not_2_out), .in3(xor_1_out), .out(multiplexer_2_out), .sel(S1_S0));
  Multiplexer #(.select(2), .width(8), .enable("false")) multiplexer_3 (
    .in0(in_6), .in1({in_6[6:0], IL}), .in2({IR, in_6[7:1]}), .out(multiplexer_3_out), .sel(SH));  // open: in3
  Multiplexer #(.width(8), .enable("false")) multiplexer_4 (
    .in0(multiplexer_3_out), .in1(multiplexer_5_out), .out(Y), .sel(S4));
  Multiplexer #(.width(8), .enable("false")) multiplexer_5 (
    .in0(adder_1_out), .in1(multiplexer_2_out), .out(multiplexer_5_out), .sel(S2));

  assign SOL = in_6[7];
  assign SOR = in_6[0];

  // Notes on the sheet:
  //   A
  //   B
  //   D
endmodule

module FunctionUnitWithState (
  input  Cin,
  input  [7:0] in_2,
  input  [7:0] in_3,
  input  [1:0] S1_S0,
  input  S2,
  input  S3,
  output [7:0] Y,
  output OV,
  output SG,
  output CA,
  output ZO
);

  wire adder_1_cout, adder_2_cout, multiplexer_6_out;
  wire [6:0] adder_1_out;
  wire [7:0] and_1_out, multiplexer_1_out, multiplexer_2_out, multiplexer_3_out, multiplexer_5_out,
       not_1_out, not_2_out, or_1_out, xor_1_out;

  assign not_1_out = ~in_3;  // NOT_Gate not_1, 8 bits wide
  Multiplexer #(.select(2), .width(8), .enable("false")) multiplexer_1 (
    .in0(in_3), .in1(not_1_out), .in2({8{1'b0}}), .in3({8{1'b1}}), .out(multiplexer_1_out), .sel(S1_S0));
  assign and_1_out = in_2 & in_3;  // AND_Gate and_1, 8 bits wide
  assign or_1_out = in_2 | in_3;  // OR_Gate or_1, 8 bits wide
  assign not_2_out = ~in_2;  // NOT_Gate not_2, 8 bits wide
  assign xor_1_out = in_2 ^ in_3;  // XOR_Gate xor_1, 8 bits wide
  Adder #(.width(7)) adder_1 (
    .a(in_2[6:0]), .b(multiplexer_1_out[6:0]), .out(adder_1_out), .cin(Cin), .cout(adder_1_cout));
  Adder #(.width(1)) adder_2 (.a(in_2[7]), .b(multiplexer_1_out[7]), .out(SG), .cin(adder_1_cout), .cout(adder_2_cout));
  Multiplexer #(.select(2), .width(8), .enable("false")) multiplexer_2 (
    .in0(and_1_out), .in1(or_1_out), .in2(not_2_out), .in3(xor_1_out), .out(multiplexer_2_out), .sel(S1_S0));
  Multiplexer #(.select(2), .width(8), .enable("false")) multiplexer_3 (
    .in0(in_3), .in1({in_3[6:0], 1'b0}), .in2({1'b0, in_3[7:1]}), .in3({{2{in_3[7]}}, in_3[6:1]}),
    .out(multiplexer_3_out), .sel(S1_S0));
  Multiplexer #(.width(8), .enable("false")) multiplexer_4 (
    .in0(multiplexer_3_out), .in1(multiplexer_5_out), .out(Y), .sel(S3));
  Multiplexer #(.width(8), .enable("false")) multiplexer_5 (
    .in0({SG, adder_1_out}), .in1(multiplexer_2_out), .out(multiplexer_5_out), .sel(S2));
  Multiplexer #(.select(2), .enable("false")) multiplexer_6 (
    .in0(1'b0), .in1(in_3[7]), .in2(in_3[0]), .in3(in_3[0]), .out(multiplexer_6_out), .sel(S1_S0));
  xor xor_2 (OV, adder_1_cout, adder_2_cout);
  Multiplexer #(.enable("false")) multiplexer_7 (.in0(multiplexer_6_out), .in1(adder_2_cout), .out(CA), .sel(S3));
  nor nor_1 (ZO, multiplexer_5_out[0], multiplexer_5_out[1], multiplexer_5_out[2], multiplexer_5_out[3], multiplexer_5_out[4], multiplexer_5_out[5], multiplexer_5_out[6], multiplexer_5_out[7]);

  // Notes on the sheet:
  //   A
  //   B
  //   D
  //   SOL
  //   SOR
endmodule

module EN (
  input  \C时钟 ,
  input  \D数据 ,
  input  \EN送数使能 ,
  output \Q输出 
);

  wire multiplexer_1_out;

  D_Flip_Flop d_ff_1 (.clk(\C时钟 ), .D(multiplexer_1_out), .Q(\Q输出 ));  // open: Qn, preset, en, reset
  Multiplexer #(.enable("false")) multiplexer_1 (.in0(\Q输出 ), .in1(\D数据 ), .out(multiplexer_1_out), .sel(\EN送数使能 ));
endmodule

module EN2 (
  input  \C时钟 ,
  input  \EN使能 ,
  input  \D数据 ,
  output \Q输出 
);

  wire and_1_out;

  and and_1 (and_1_out, \C时钟 , \EN使能 );
  D_Flip_Flop d_ff_1 (.clk(and_1_out), .D(\D数据 ), .Q(\Q输出 ));  // open: Qn, preset, en, reset
endmodule

module Regs (
  input  [7:0] \Din_待写入数据 ,
  input  [1:0] \ADDR_选择寄存器 ,
  input  [1:0] \SB_B选择输出 ,
  input  \nR_W是否写 ,
  input  [1:0] \SA_A选择输出 ,
  input  \CLK时钟 ,
  output [7:0] \A_待输出数据 ,
  output [7:0] \B_待输出数据 
);

  wire and_1_out, and_2_out, and_3_out, and_4_out, decoder_1_out0, decoder_1_out1, decoder_1_out2,
       decoder_1_out3;
  wire [7:0] register_1_q, register_2_q, register_3_q, register_4_q;

  Decoder #(.select(2), .enable("false")) decoder_1 (
    .out0(decoder_1_out0), .out1(decoder_1_out1), .out2(decoder_1_out2), .out3(decoder_1_out3),
    .sel(\ADDR_选择寄存器 ));
  and and_1 (and_1_out, \nR_W是否写 , decoder_1_out0);
  and and_2 (and_2_out, \nR_W是否写 , decoder_1_out1);
  and and_3 (and_3_out, \nR_W是否写 , decoder_1_out2);
  and and_4 (and_4_out, \nR_W是否写 , decoder_1_out3);
  Register register_1 (.D(\Din_待写入数据 ), .en(and_1_out), .Q(register_1_q), .clk(\CLK时钟 ));  // open: clr
  Register register_2 (.D(\Din_待写入数据 ), .en(and_2_out), .Q(register_2_q), .clk(\CLK时钟 ));  // open: clr
  Register register_3 (.D(\Din_待写入数据 ), .en(and_3_out), .Q(register_3_q), .clk(\CLK时钟 ));  // open: clr
  Register register_4 (.D(\Din_待写入数据 ), .en(and_4_out), .Q(register_4_q), .clk(\CLK时钟 ));  // open: clr
  Multiplexer #(.select(2), .width(8), .enable("false")) multiplexer_1 (
    .in0(register_1_q), .in1(register_2_q), .in2(register_3_q), .in3(register_4_q), .out(\A_待输出数据 ),
    .sel(\SA_A选择输出 ));
  Multiplexer #(.select(2), .width(8), .enable("false")) multiplexer_2 (
    .in0(register_1_q), .in1(register_2_q), .in2(register_3_q), .in3(register_4_q), .out(\B_待输出数据 ),
    .sel(\SB_B选择输出 ));
endmodule

module CU (
  input  \TC_转到下一指令 ,
  input  RST,
  input  O,
  input  S,
  input  C,
  input  Z,
  input  \TA_执行指令 ,
  input  [15:0] \PDIN_程序数据 ,
  input  \TF_取指令 ,
  output [7:0] \PADDR_程序地址 ,
  output W,
  output CI,
  output RM,
  output WM,
  output SF,
  output JP,
  output [4:0] FS,
  output [7:0] ADDRIM
);

  wire and_1_out, multiplexer_1_out, nor_1_out;
  wire [3:0] register_1_q;
  wire [7:0] adder_1_out, multiplexer_2_out;

  Register #(.width(4)) register_1 (.D({Z, C, S, O}), .en(SF), .Q(register_1_q), .clk(\TA_执行指令 ));  // open: clr
  Register PC (.D(adder_1_out), .Q(\PADDR_程序地址 ), .clk(\TC_转到下一指令 ), .clr(RST));  // open: en
  Multiplexer #(.select(3), .enable("false")) multiplexer_1 (
    .in0(1'b1), .in1(register_1_q[0]), .in2(register_1_q[1]), .in3(register_1_q[2]), .in4(register_1_q[3]),
    .out(multiplexer_1_out), .sel(FS[3:1]));  // open: in5, in6, in7
  Register #(.width(16)) IR (.D(\PDIN_程序数据 ), .Q({JP, RM, CI, FS, ADDRIM}), .clk(\TF_取指令 ));  // open: en, clr
  Multiplexer #(.width(8), .enable("false")) multiplexer_2 (
    .in0(8'h1), .in1(ADDRIM), .out(multiplexer_2_out), .sel(and_1_out));
  and and_1 (and_1_out, multiplexer_1_out, JP);
  Adder adder_1 (.a(\PADDR_程序地址 ), .b(multiplexer_2_out), .out(adder_1_out));  // open: cin, cout
  nor nor_1 (nor_1_out, JP, RM);
  and and_2 (WM, RM, ~CI);  // AND_Gate
  nor nor_2 (SF, JP, RM);
  or or_1 (W, nor_1_out, CI);
endmodule

module OPdecoder (
  input  [15:0] IND,
  output W,
  output CI,
  output RM,
  output WM,
  output SF,
  output JP,
  output [4:0] OPCODE,
  output [7:0] ADDRIM
);

  wire nor_1_out;

  nor nor_1 (nor_1_out, IND[0], IND[1]);
  or or_1 (W, nor_1_out, IND[2]);
  and and_1 (WM, IND[1], ~IND[2]);  // AND_Gate
  nor nor_2 (SF, IND[0], IND[1]);

  assign ADDRIM = IND[15:8];
  assign CI = IND[2];
  assign JP = IND[0];
  assign OPCODE = IND[7:3];
  assign RM = IND[1];
endmodule
